# Fritzing sketch uhppoted-wiegand-pico-v1 (saved by Fritzing 0.9.10b)
breadboards: 4

parts:
  M1 = RioRand LM2596
  Part1 = Adafruit 4-channel I2C-safe Bi-directional Logic Level Converter [part_number="Adafruit #757"]
  LED3 = LED - 3mm [color="Orange (620nm)" current=0.030 package="3 mm [THT]"]
  LED4 = LED - 3mm [color="Red (633nm)" current=0.030 package="3 mm [THT]"]
  LED1 = LED - 3mm [color="Green (555nm)" current=0.030 package="3 mm [THT]"]
  R4 = Resistor [tolerance=±5% resistance=1k package="0402 [SMD]"]
  LED2 = LED - 3mm [color="Yellow (585nm)" current=0.030 package="3 mm [THT]"]
  BZR1 = Piezo Speaker
  J4 = female pin header, 2 pins [form="♀ (female)"]
  Mod1 = Raspberry Pi Pico
  Part2 = Adafruit SDIO microSD Breakout
  R5 = Resistor [tolerance=±5% resistance=1k package="0402 [SMD]"]
  J6 = Camdenboss CTB0158-2 [part_number=CTB0158-2 package=THT]
  J7 = Camdenboss CTB0158-5 [part_number=CTB0158-5 package=THT]
  R6 = Resistor [tolerance=±5% power=0.25 resistance=1k package=THT]
  J9 = Camdenboss CTB0158-2 [part_number=CTB0158-2 package=THT]
  Mod2 = KY-019 5V Relay Module [package="Breakout board"]
  DPDT_Relay1 = DPDT Relay [chip_label=Relay package="DIP (Dual Inline) [THT]"]
  DPDT_Relay2 = DPDT Relay [chip_label=Relay package="DIP (Dual Inline) [THT]"]
  J10 = Camdenboss CTB0158-2 [part_number=CTB0158-2 package=THT]
  J8 = Camdenboss CTB0158-3 [part_number=CTB0158-3 package=THT]
  IC1 = IC, DIP package, 20 pins [chip_label=TPIC6B595]
  Part3 = TXB0104 4-channel Bi-Directional Level Shifter
  R11 = Resistor [tolerance=±5% power=0.25 resistance=220 package=THT]
  R12 = Resistor [tolerance=±5% power=0.25 resistance=10k package=THT]
  R13 = Resistor [tolerance=±5% power=0.25 resistance=10k package=THT]
  Part4 = Adafruit 4-channel I2C-safe Bi-directional Logic Level Converter [part_number="Adafruit #757"]
  R7 = Resistor [tolerance=±5% power=0.25 resistance=1k package=THT]
  R2 = Resistor [tolerance=±5% resistance=1k power=0.25 package=THT]
  R1 = Resistor [tolerance=±5% resistance=1k power=0.25 package=THT]
  R3 = Resistor [tolerance=±5% resistance=1k power=0.25 package=THT]

nets:
  12V: M1.Pin_1, J6.pin1, J7.pin1
  GND: M1.Pin_2, M1.Pin_4, Part1.GND, Mod1.pin_3, Mod1.pin_8, Mod1.pin_11, Mod1.pin_13, Mod1.pin_18, Mod1.pin_23, Mod1.pin_28, Mod1.pin_33, Mod1.pin_38, Part2.GND, J6.pin2, J7.pin2, Mod2.-, DPDT_Relay1.pin4, DPDT_Relay2.pin4, J8.pin1, IC1.pin10, IC1.pin11, IC1.pin20, Part3.GND, R11.Pin_1, Part4.GND
  5V: M1.Pin_3, Part1.HV, R4.Pin_1, Mod1.pin_39, R6.Pin_0, Mod2.+, DPDT_Relay1.pin8, DPDT_Relay2.pin8, IC1.pin1, Part3.HV, R12.Pin_1, R13.Pin_1, Part4.HV, R7.Pin_0, R2.Pin_1, R1.Pin_1, R3.Pin_1
  N1: Part1.A4, Mod1.pin_25
  N2: Part1.A3, Mod1.pin_26, Mod1.pin_27
  N3: Part1.A2, Mod1.pin_29, Mod1.pin_31
  N4: Part1.A1, Mod1.pin_32, Mod1.pin_34
  3.3V: Part1.LV, BZR1.pin2, Mod1.pin_36, Part2.3.3V, Part3.LV, Part4.LV
  N5: Part1.B4, Mod2.S
  N6: Part1.B3, J7.pin5
  N7: Part1.B2, J7.pin4
  N8: Part1.B1, J7.pin3
  N9: LED3.cathode, IC1.pin15
  N10: LED3.anode, R3.Pin_0
  N11: LED4.cathode, IC1.pin14
  N12: LED4.anode, R4.Pin_0
  N13: LED1.cathode, IC1.pin17
  N14: LED1.anode, R1.Pin_0
  N15: LED2.cathode, IC1.pin16
  N16: LED2.anode, R2.Pin_0
  N17: BZR1.pin1, R5.Pin_0
  N18: J4.pin1, Mod1.pin_2
  N19: J4.pin2, Mod1.pin_1
  N20: Mod1.pin_4, Part2.SCLK
  N21: Mod1.pin_5, Part2.DI
  N22: Mod1.pin_6, Part2.DO
  N23: Mod1.pin_7, Part2.CS
  N24: Mod1.pin_9, Part2.CARDDET
  N25: Mod1.pin_12, R5.Pin_1
  N26: Mod1.pin_14, Part3.A1
  N27: Mod1.pin_15, Part3.A2
  N28: Mod1.pin_16, Part3.A3
  N29: Mod1.pin_17, Part3.A4
  N30: Mod1.pin_19, Part4.A3
  N31: Mod1.pin_20, Part4.A4
  N32: Mod1.pin_21, Part4.A2
  N33: Mod1.pin_22, Part4.A1
  N34: R6.Pin_1, J8.pin3, Part4.B2
  N35: J9.pin1, DPDT_Relay1.pin7
  N36: J9.pin2, DPDT_Relay1.pin5
  N37: DPDT_Relay1.pin1, IC1.pin7
  N38: DPDT_Relay1.pin2, R12.Pin_0, Part4.B3
  N39: DPDT_Relay2.pin1, IC1.pin6
  N40: DPDT_Relay2.pin2, R13.Pin_0, Part4.B4
  N41: DPDT_Relay2.pin5, J10.pin2
  N42: DPDT_Relay2.pin7, J10.pin1
  N43: J8.pin2, Part4.B1, R7.Pin_1
  N44: IC1.pin3, Part3.B2
  N45: IC1.pin9, Part3.B1
  N46: IC1.pin13, Part3.B4
  N47: IC1.pin18, Part3.B3
  N48: Part3.OE, R11.Pin_0

custom parts:
  Adafruit 4-channel I2C-safe Bi-directional Logic Level Converter: Because the Arduino (and Basic Stamp) are 5V devices, and most modern sensors, displays, flash cards and modes are 3.3V-only, many makers find that they need to perform level shifting/conversion to protect the 3.3V device from 5V. We do have some other handy level shifters in the shop, from the DIP 74LVC245 to the fancy bi-directional TXB0108. However, neither of these are happy to work with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
  Raspberry Pi Pico: Raspberry Pi Pico. Based around the RP2040 microcontroller the Pico is a low cost microcontroller device bringing Raspberry Pi quality, cost, and easy of use to the microcontroller space. Jan 2021, Split part in to two versions: tht (this one) and SMD. This one will drill holes for a .1 in header in pcb to allow plugging in the module as well as providing pads to solder the module to the top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
  KY-019 5V Relay Module: KY-019 5V Relay module, used to control AC circuits. (Special thanks to vanepp for fixing the PCB holes and other errors)
  DPDT Relay: DIP DPDT Relay (Double Pole Double Throw)
  TXB0104 4-channel Bi-Directional Level Shifter: Because the Arduino (and Basic Stamp) are 5V devices, and most modern sensors, displays, flash cards and modes are 3.3V-only, many makers find that they need to perform level shifting/conversion to protect the 3.3V device from 5V. Although one can use resistors to make a divider, for high speed transfers, the resistors can add a lot of slew and cause havoc that is tough to debug. For that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
